// Logisim project DPS.circ as structural Verilog: 1 circuit, main circuit main
module main (
  input  in_1,
  input  in_2,
  input  in_3,
  input  in_4,
  input  in_5,
  input  in_6,
  input  in_7,
  input  And_using_Nand,
  input  in_9,
  input  in_10,
  input  Or_using_Nor,
  input  in_12,
  input  in_13,
  input  in_14,
  input  in_15,
  input  in_16,
  input  in_17,
  input  in_18,
  output out_19,
  output out_20,
  output out_21,
  output out_22,
  output out_23,
  output out_24,
  output out_25,
  output out_26,
  output out_27,
  output out_28
);

  wire nand_2_out, nand_3_out, nand_4_out, nand_8_out, nand_9_out, nand_10_out, nor_2_out, nor_3_out,
       nor_4_out, nor_5_out, nor_6_out, nor_7_out, nor_8_out;

  nand nand_1 (out_19, in_1, in_3);
  nor nor_1 (out_22, in_5, in_7);
  nand nand_2 (nand_2_out, And_using_Nand, in_10);
  nand nand_3 (nand_3_out, in_13, in_13);
  nand nand_4 (nand_4_out, in_16, in_16);
  nand nand_5 (out_23, nand_2_out, nand_2_out);
  nand nand_6 (out_26, nand_3_out, nand_4_out);
  nor nor_2 (nor_2_out, Or_using_Nor, in_12);
  nor nor_3 (nor_3_out, in_17, in_17);
  nor nor_4 (nor_4_out, in_18, in_18);
  nor nor_5 (nor_5_out, in_18, in_17);
  nor nor_6 (nor_6_out, in_2, in_2);
  nor nor_7 (nor_7_out, in_6, in_6);
  nand nand_7 (out_27, in_15, in_15);
  nor nor_8 (nor_8_out, nor_3_out, nor_4_out);
  nor nor_9 (out_21, nor_6_out, nor_7_out);
  nor nor_10 (out_24, nor_2_out, nor_2_out);
  nor nor_11 (out_28, nor_8_out, nor_5_out);
  nand nand_8 (nand_8_out, in_9, in_14);
  nor nor_12 (out_20, in_4, in_4);
  nand nand_9 (nand_9_out, in_9, nand_8_out);
  nand nand_10 (nand_10_out, nand_8_out, in_14);
  nand nand_11 (out_25, nand_9_out, nand_10_out);

  // Notes on the sheet:
  //   Or using Nand
  //   Nand Gate
  //   NOR graph
  //   xOR using Nor
  //   not using Nand
  //   And using NOR
  //   not using Nor
  //   Xor using Nand
endmodule
