// Logisim project p-4.circ as structural Verilog: 1 circuit, main circuit main
module main (
  input  in_1,
  input  in_2,
  input  in_3,
  input  in_4,
  input  in_5,
  input  in_6,
  input  in_7,
  input  in_8,
  output s,
  output out_10,
  output c,
  output out_12,
  output out_13,
  output out_14
);

  wire and_2_out, and_3_out, xor_2_out;

  xor xor_1 (s, in_2, in_4);
  and and_1 (c, in_2, in_4);
  xor xor_2 (xor_2_out, in_6, in_7);
  and and_2 (and_2_out, in_6, in_7);
  and and_3 (and_3_out, xor_2_out, in_8);
  xor xor_3 (out_13, xor_2_out, in_8);
  or or_1 (out_14, and_2_out, and_3_out);
  Adder #(.width(1)) adder_1 (.a(in_3), .b(in_5), .out(out_10), .cin(in_1), .cout(out_12));

  // Notes on the sheet:
  //   Half adder
  //   Full adder
  //   s
  //   c
  //   Adder
endmodule
