// Logisim project 6.11.circ as structural Verilog: 1 circuit, main circuit main
module main (
  input  S1,
  input  S0,
  input  D,
  input  in_4,
  output O0,
  output O1,
  output out_7,
  output O3
);

  wire not_1_out, not_2_out, not_3_out;

  not not_1 (not_1_out, S1);
  not not_2 (not_2_out, in_4);
  not not_3 (not_3_out, S0);
  and and_1 (O0, not_1_out, not_3_out, D, not_2_out);
  and and_2 (O1, not_1_out, S0, D, not_2_out);
  and and_3 (out_7, S1, not_3_out, D, not_2_out);
  and and_4 (O3, S1, S0, D, not_2_out);

  // Notes on the sheet:
  //   O2
endmodule
