// Logisim project 6.circ as structural Verilog: 1 circuit, main circuit main
// 2
module main (
  input  S1,
  input  S0,
  input  I3,
  input  I2,
  input  I1,
  input  I0,
  input  in_7,
  input  in_8,
  input  in_9,
  output out_10
);

  wire and_1_out, and_2_out, and_3_out, and_4_out, not_1_out, not_2_out, not_3_out;
  wire [1:1] undriven;

  not not_1 (not_1_out, S1);
  not not_2 (not_2_out, in_7);
  not not_3 (not_3_out, S0);
  Multiplexer #(.select(2), .width(2)) multiplexer_1 (
    .sel({undriven[1], in_8}), .en(in_9));  // open: in0, in1, in2, in3, out
  and and_1 (and_1_out, I0, not_1_out, not_1_out, not_2_out);
  and and_2 (and_2_out, not_1_out, S0, I1, not_2_out);
  and and_3 (and_3_out, S1, not_3_out, I2, not_2_out);
  and and_4 (and_4_out, S1, S0, I3, not_2_out);
  or or_1 (out_10, and_1_out, and_2_out, and_3_out, and_4_out);
  // Pins of 1 and 2 bits meet at {undriven[1], in_8}

  // Notes on the sheet:
  //   Multiplexer
  //   I0
  //   I1
  //   I2
  //   I3
endmodule
