// Logisim project 7.circ as structural Verilog: 1 circuit, main circuit main
module main (
  input  in_1,
  input  in_2,
  input  in_3,
  input  [1:0] in_4,
  input  in_5,
  input  in_6,
  input  in_7,
  input  in_8,
  input  in_9,
  input  in_10,
  input  in_11,
  output out_12,
  output out_13,
  output out_14,
  output out_15,
  output out_16,
  output out_17,
  output out_18,
  output [1:0] out_19
);

  Multiplexer multiplexer_1 (.in0(in_1), .in1(in_2), .out(out_14), .sel(in_3));  // open: en
  Demultiplexer demultiplexer_1 (.out0(out_17), .out1(out_18), .in(in_7), .sel(in_11), .en(in_9));
  Priority_Encoder #(.select(2)) priority_encoder_1 (
    .in0(in_5), .in1(in_6), .in2(in_8), .in3(in_10), .out(out_19));  // open: gs, en_out, en_in
  Decoder #(.select(2)) decoder_1 (.out0(out_12), .out1(out_13), .out2(out_15), .out3(out_16), .sel(in_4));  // open: en
endmodule
